// Logisim project Compu.circ as structural Verilog: 1 circuit, main circuit main
module main (
);

  wire and_1_out, and_3_out, clock_1_out, comparator_1_eq, comparator_1_gt, comparator_1_lt, comparator_2_eq,
       comparator_3_eq, comparator_4_eq, CONDITION_q, d_ff_1_q, demultiplexer_1_out0, demultiplexer_1_out1,
       demultiplexer_1_out2, demultiplexer_1_out3, demultiplexer_1_out4, demultiplexer_1_out5,
       demultiplexer_1_out6, demultiplexer_1_out7, demultiplexer_1_out8, demultiplexer_1_out9,
       demultiplexer_1_out10, demultiplexer_1_out11, demultiplexer_1_out12, demultiplexer_1_out13,
       demultiplexer_1_out14, demultiplexer_1_out15, demultiplexer_1_out16, demultiplexer_1_out17,
       demultiplexer_1_out18, demultiplexer_1_out19, demultiplexer_2_out0, demultiplexer_2_out1,
       demultiplexer_3_out0, demultiplexer_3_out1, multiplexer_7_out, not_1_out, not_2_out, not_3_out,
       register_1_q, RESET_out;
  wire [1:0] PC_JUMP_OP_q;
  wire [3:0] ALU_OP_q, binary_to_bcd_converter_1_p2, binary_to_bcd_converter_1_p3,
       binary_to_bcd_converter_1_p4, binary_to_bcd_converter_2_p2, binary_to_bcd_converter_2_p3,
       binary_to_bcd_converter_2_p4, binary_to_bcd_converter_3_p1, binary_to_bcd_converter_3_p3,
       binary_to_bcd_converter_3_p4, binary_to_bcd_converter_3_p5, binary_to_bcd_converter_4_p1,
       binary_to_bcd_converter_4_p3, binary_to_bcd_converter_4_p4, binary_to_bcd_converter_4_p5,
       binary_to_bcd_converter_5_p1, binary_to_bcd_converter_5_p3, binary_to_bcd_converter_5_p4,
       binary_to_bcd_converter_5_p5, binary_to_bcd_converter_5_p6, binary_to_bcd_converter_6_p1,
       binary_to_bcd_converter_6_p3, binary_to_bcd_converter_6_p4, binary_to_bcd_converter_6_p5,
       binary_to_bcd_converter_6_p6, binary_to_bcd_converter_7_p2, binary_to_bcd_converter_7_p3,
       binary_to_bcd_converter_7_p4, binary_to_bcd_converter_8_p1, binary_to_bcd_converter_8_p3,
       binary_to_bcd_converter_8_p4, binary_to_bcd_converter_8_p5, binary_to_bcd_converter_9_p1,
       binary_to_bcd_converter_9_p3, binary_to_bcd_converter_9_p4, binary_to_bcd_converter_9_p5,
       binary_to_bcd_converter_9_p6;
  wire [6:0] GPU_INSTRUCTION_dout;
  wire [7:0] multiplexer_6_out;
  wire [9:0] GPU_INS_ADR_q, GPU_PC_q_2, multiplexer_1_out, multiplexer_1_out_2, multiplexer_4_out;
  wire [10:0] GPU_PC_q;
  wire [11:0] binary_to_bcd_converter_2_p1, multiplexer_1_out_3;
  wire [19:0] ALU_X_q;
  wire [23:0] END_DIR_q, multiplexer_2_out, multiplexer_3_out, multiplexer_5_out, PC_q, rgb_video_1_p6,
       STACK_PC_ADR_q, STACK_PC_dout, START_DIR_q;
  wire [31:0] adder_1_out, ALU_Y_q, and_2_out, bit_extender_1_out, bit_extender_2_out, bit_extender_3_out,
       divider_1_out, Instructions_data, multiplier_1_out, nand_1_out, nor_1_out, or_1_out, R0_q, R1_q, R2_q,
       R3_q, R4_q, R5_q, R6_q, R7_q, subtractor_1_out, xnor_1_out, xor_1_out;
  wire [31:24] multiplexer_2_out_2;
  wire [41:32] Instructions_data_2;
  wire [63:0] Resources_data;

  Clock clock_1 (.out(clock_1_out));
  Button RESET (.out(RESET_out));
  Hex_Digit_Display hex_digit_display_1 (.value(binary_to_bcd_converter_1_p2));  // open: dp
  // Binary_to_BCD_converter #(.binvalue(12)) binary_to_bcd_converter_1: pin names not known; wires that end beside it: ALU_Y_q[31:20], binary_to_bcd_converter_1_p2, binary_to_bcd_converter_1_p3, binary_to_bcd_converter_1_p4
  Hex_Digit_Display hex_digit_display_2 (.value(binary_to_bcd_converter_2_p2));  // open: dp
  // Binary_to_BCD_converter #(.binvalue(12)) binary_to_bcd_converter_2: pin names not known; wires that end beside it: binary_to_bcd_converter_2_p1, binary_to_bcd_converter_2_p2, binary_to_bcd_converter_2_p3, binary_to_bcd_converter_2_p4
  D_Flip_Flop d_ff_1 (.D(RESET_out), .clk(clock_1_out), .Q(d_ff_1_q));  // open: Qn, preset, reset
  Hex_Digit_Display hex_digit_display_3 (.value(binary_to_bcd_converter_1_p3));  // open: dp
  Hex_Digit_Display hex_digit_display_4 (.value(binary_to_bcd_converter_1_p4));  // open: dp
  Hex_Digit_Display hex_digit_display_5 (.value(binary_to_bcd_converter_2_p3));  // open: dp
  Hex_Digit_Display hex_digit_display_6 (.value(binary_to_bcd_converter_2_p4));  // open: dp
  Register #(.width(32)) ALU_X (
    .D({multiplexer_2_out_2, multiplexer_2_out}), .en(demultiplexer_1_out0), .clk(clock_1_out),
    .Q({binary_to_bcd_converter_2_p1, ALU_X_q}), .clr(and_1_out));
  Register #(.width(32)) ALU_Y (
    .D({multiplexer_2_out_2, multiplexer_2_out}), .en(demultiplexer_1_out1), .clk(clock_1_out), .Q(ALU_Y_q),
    .clr(and_1_out));
  not not_1 (not_1_out, d_ff_1_q);
  Hex_Digit_Display hex_digit_display_7 (.value(binary_to_bcd_converter_3_p1));  // open: dp
  Hex_Digit_Display hex_digit_display_8 (.value(binary_to_bcd_converter_4_p1));  // open: dp
  and and_1 (and_1_out, RESET_out, not_1_out);
  Hex_Digit_Display hex_digit_display_9 (.value(binary_to_bcd_converter_3_p3));  // open: dp
  // Binary_to_BCD_converter #(.binvalue(10)) binary_to_bcd_converter_3: pin names not known; wires that end beside it: binary_to_bcd_converter_3_p1, ALU_Y_q[19:10], binary_to_bcd_converter_3_p3, binary_to_bcd_converter_3_p4, binary_to_bcd_converter_3_p5
  Hex_Digit_Display hex_digit_display_10 (.value(binary_to_bcd_converter_4_p3));  // open: dp
  // Binary_to_BCD_converter #(.binvalue(10)) binary_to_bcd_converter_4: pin names not known; wires that end beside it: binary_to_bcd_converter_4_p1, ALU_X_q[19:10], binary_to_bcd_converter_4_p3, binary_to_bcd_converter_4_p4, binary_to_bcd_converter_4_p5
  Adder #(.width(32)) adder_1 (
    .a({binary_to_bcd_converter_2_p1, ALU_X_q}), .b(ALU_Y_q), .out(adder_1_out));  // open: cin, cout
  Subtractor #(.width(32)) subtractor_1 (
    .a({binary_to_bcd_converter_2_p1, ALU_X_q}), .b(ALU_Y_q), .out(subtractor_1_out));  // open: bin, bout
  Multiplier #(.width(32)) multiplier_1 (
    .a({binary_to_bcd_converter_2_p1, ALU_X_q}), .b(ALU_Y_q), .out(multiplier_1_out));  // open: cin, cout
  Divider #(.width(32)) divider_1 (
    .a({binary_to_bcd_converter_2_p1, ALU_X_q}), .b(ALU_Y_q), .out(divider_1_out));  // open: upper, rem
  assign and_2_out = {binary_to_bcd_converter_2_p1, ALU_X_q} & ALU_Y_q;  // AND_Gate and_2, 32 bits wide
  assign nand_1_out = ~({binary_to_bcd_converter_2_p1, ALU_X_q} & ALU_Y_q);  // NAND_Gate nand_1, 32 bits wide
  assign or_1_out = {binary_to_bcd_converter_2_p1, ALU_X_q} | ALU_Y_q;  // OR_Gate or_1, 32 bits wide
  assign nor_1_out = ~({binary_to_bcd_converter_2_p1, ALU_X_q} | ALU_Y_q);  // NOR_Gate nor_1, 32 bits wide
  assign xor_1_out = {binary_to_bcd_converter_2_p1, ALU_X_q} ^ ALU_Y_q;  // XOR_Gate xor_1, 32 bits wide
  assign xnor_1_out = ~({binary_to_bcd_converter_2_p1, ALU_X_q} ^ ALU_Y_q);  // XNOR_Gate xnor_1, 32 bits wide
  assign bit_extender_1_out = {{31{1'b0}}, comparator_1_gt};  // Bit_Extender bit_extender_1
  assign bit_extender_2_out = {{31{1'b0}}, comparator_1_eq};  // Bit_Extender bit_extender_2
  Comparator #(.mode("unsigned"), .width(32)) comparator_1 (
    .a({binary_to_bcd_converter_2_p1, ALU_X_q}), .b(ALU_Y_q), .gt(comparator_1_gt), .eq(comparator_1_eq),
    .lt(comparator_1_lt));
  assign bit_extender_3_out = {{31{1'b0}}, comparator_1_lt};  // Bit_Extender bit_extender_3
  Hex_Digit_Display hex_digit_display_11 (.value(binary_to_bcd_converter_3_p4));  // open: dp
  Hex_Digit_Display hex_digit_display_12 (.value(binary_to_bcd_converter_4_p4));  // open: dp
  Register #(.width(4)) ALU_OP (
    .D(multiplexer_2_out[3:0]), .en(demultiplexer_1_out16), .clk(clock_1_out), .Q(ALU_OP_q), .clr(and_1_out));
  Hex_Digit_Display hex_digit_display_13 (.value(binary_to_bcd_converter_3_p5));  // open: dp
  Hex_Digit_Display hex_digit_display_14 (.value(binary_to_bcd_converter_5_p1));  // open: dp
  Hex_Digit_Display hex_digit_display_15 (.value(binary_to_bcd_converter_4_p5));  // open: dp
  Hex_Digit_Display hex_digit_display_16 (.value(binary_to_bcd_converter_6_p1));  // open: dp
  Demultiplexer #(.select(5)) demultiplexer_1 (
    .out0(demultiplexer_1_out0), .out1(demultiplexer_1_out1), .out2(demultiplexer_1_out2),
    .out3(demultiplexer_1_out3), .out4(demultiplexer_1_out4), .out5(demultiplexer_1_out5),
    .out6(demultiplexer_1_out6), .out7(demultiplexer_1_out7), .out8(demultiplexer_1_out8),
    .out9(demultiplexer_1_out9), .out10(demultiplexer_1_out10), .out11(demultiplexer_1_out11),
    .out12(demultiplexer_1_out12), .out13(demultiplexer_1_out13), .out14(demultiplexer_1_out14),
    .out15(demultiplexer_1_out15), .out16(demultiplexer_1_out16), .out17(demultiplexer_1_out17),
    .out18(demultiplexer_1_out18), .out19(demultiplexer_1_out19), .in(Instructions_data_2[36]),
    .sel(Instructions_data_2[41:37]));  // open: out20, out21, out22, out23, out24, out25, out26, out27, out28, out29, out30, out31
  Register #(.width(1)) register_1 (.D(not_2_out), .en(1'b1), .clk(clock_1_out), .Q(register_1_q), .clr(and_1_out));
  Hex_Digit_Display hex_digit_display_17 (.value(binary_to_bcd_converter_5_p3));  // open: dp
  // Binary_to_BCD_converter #(.binvalue(10)) binary_to_bcd_converter_5: pin names not known; wires that end beside it: binary_to_bcd_converter_5_p1, ALU_Y_q[9:0], binary_to_bcd_converter_5_p3, binary_to_bcd_converter_5_p4, binary_to_bcd_converter_5_p5, binary_to_bcd_converter_5_p6
  Hex_Digit_Display hex_digit_display_18 (.value(binary_to_bcd_converter_6_p3));  // open: dp
  // Binary_to_BCD_converter #(.binvalue(10)) binary_to_bcd_converter_6: pin names not known; wires that end beside it: binary_to_bcd_converter_6_p1, ALU_X_q[9:0], binary_to_bcd_converter_6_p3, binary_to_bcd_converter_6_p4, binary_to_bcd_converter_6_p5, binary_to_bcd_converter_6_p6
  Multiplexer #(.select(4), .width(32)) multiplexer_1 (
    .in0(adder_1_out), .in1(subtractor_1_out), .in2(multiplier_1_out), .in3(divider_1_out), .in4(and_2_out),
    .in5(nand_1_out), .in6(or_1_out), .in7(nor_1_out), .in8(xor_1_out), .in9(xnor_1_out),
    .in10(bit_extender_1_out), .in11(bit_extender_2_out), .in12(bit_extender_3_out),
    .out({multiplexer_1_out_3, multiplexer_1_out_2, multiplexer_1_out}), .sel(ALU_OP_q));  // open: in13, in14, in15
  Comparator #(.mode("unsigned"), .width(1)) comparator_2 (
    .a(register_1_q), .b(1'b1), .eq(comparator_2_eq));  // open: gt, lt
  not not_2 (not_2_out, register_1_q);
  not not_3 (not_3_out, comparator_3_eq);
  Comparator #(.mode("unsigned"), .width(1)) comparator_3 (.a(1'b0), .b(1'b1), .eq(comparator_3_eq));  // open: gt, lt
  Hex_Digit_Display hex_digit_display_19 (.value(binary_to_bcd_converter_5_p4));  // open: dp
  Hex_Digit_Display hex_digit_display_20 (.value(binary_to_bcd_converter_6_p4));  // open: dp
  Register #(.width(32)) R0 (
    .D({multiplexer_2_out_2, multiplexer_2_out}), .en(demultiplexer_1_out2), .clk(clock_1_out), .Q(R0_q),
    .clr(and_1_out));
  and and_3 (and_3_out, comparator_2_eq, not_3_out);
  Hex_Digit_Display hex_digit_display_21 (.value(binary_to_bcd_converter_5_p5));  // open: dp
  Hex_Digit_Display hex_digit_display_22 (.value(binary_to_bcd_converter_6_p5));  // open: dp
  ROM #(.addrWidth(24), .dataWidth(42)) Instructions (.addr(PC_q), .data({Instructions_data_2, Instructions_data}));
  Counter #(.max('hffffff), .width(24)) PC (
    .load(demultiplexer_1_out15), .D(multiplexer_5_out), .count(and_3_out), .Q(PC_q), .up(1'b1),
    .clk(clock_1_out), .clr(and_1_out));  // open: carry
  Hex_Digit_Display hex_digit_display_23 (.value(binary_to_bcd_converter_5_p6));  // open: dp
  Hex_Digit_Display hex_digit_display_24 (.value(binary_to_bcd_converter_6_p6));  // open: dp
  Register #(.width(32)) R1 (
    .D({multiplexer_2_out_2, multiplexer_2_out}), .en(demultiplexer_1_out3), .clk(clock_1_out), .Q(R1_q),
    .clr(and_1_out));
  Hex_Digit_Display hex_digit_display_25 (.value(binary_to_bcd_converter_7_p2));  // open: dp
  // Binary_to_BCD_converter #(.binvalue(12)) binary_to_bcd_converter_7: pin names not known; wires that end beside it: multiplexer_1_out_3, binary_to_bcd_converter_7_p2, binary_to_bcd_converter_7_p3, binary_to_bcd_converter_7_p4
  Register #(.width(32)) R2 (
    .D({multiplexer_2_out_2, multiplexer_2_out}), .en(demultiplexer_1_out4), .clk(clock_1_out), .Q(R2_q),
    .clr(and_1_out));
  Hex_Digit_Display hex_digit_display_26 (.value(binary_to_bcd_converter_7_p3));  // open: dp
  Register #(.width(32)) R3 (
    .D({multiplexer_2_out_2, multiplexer_2_out}), .en(demultiplexer_1_out5), .clk(clock_1_out), .Q(R3_q),
    .clr(and_1_out));
  Register #(.width(24)) STACK_PC_ADR (
    .D(multiplexer_2_out), .en(demultiplexer_1_out19), .clk(and_3_out), .Q(STACK_PC_ADR_q), .clr(and_1_out));
  Hex_Digit_Display hex_digit_display_27 (.value(binary_to_bcd_converter_7_p4));  // open: dp
  Hex_Digit_Display hex_digit_display_28 (.value(binary_to_bcd_converter_8_p1));  // open: dp
  Demultiplexer demultiplexer_2 (
    .out0(demultiplexer_2_out0), .out1(demultiplexer_2_out1), .in(1'b1), .sel(demultiplexer_1_out14));
  Hex_Digit_Display hex_digit_display_29 (.value(binary_to_bcd_converter_8_p3));  // open: dp
  // Binary_to_BCD_converter #(.binvalue(10)) binary_to_bcd_converter_8: pin names not known; wires that end beside it: binary_to_bcd_converter_8_p1, multiplexer_1_out_2, binary_to_bcd_converter_8_p3, binary_to_bcd_converter_8_p4, binary_to_bcd_converter_8_p5
  Register #(.width(32)) R4 (
    .D({multiplexer_2_out_2, multiplexer_2_out}), .en(demultiplexer_1_out6), .clk(clock_1_out), .Q(R4_q),
    .clr(and_1_out));
  RAM #(.addrWidth(24), .dataWidth(24)) STACK_PC (
    .addr(STACK_PC_ADR_q), .we(demultiplexer_2_out1), .oe(demultiplexer_2_out0), .clk(clock_1_out),
    .din(multiplexer_2_out), .dout(STACK_PC_dout));
  Hex_Digit_Display hex_digit_display_30 (.value(binary_to_bcd_converter_8_p4));  // open: dp
  Register #(.width(32)) R5 (
    .D({multiplexer_2_out_2, multiplexer_2_out}), .en(demultiplexer_1_out7), .clk(clock_1_out), .Q(R5_q),
    .clr(and_1_out));
  Hex_Digit_Display hex_digit_display_31 (.value(binary_to_bcd_converter_8_p5));  // open: dp
  Multiplexer #(.select(4), .width(32)) multiplexer_2 (
    .in0({multiplexer_1_out_3, multiplexer_1_out_2, multiplexer_1_out}), .in1(R0_q), .in2(R1_q), .in3(R2_q),
    .in4(R3_q), .in5(R4_q), .in6(R5_q), .in7(R6_q), .in8(R7_q), .in9(Instructions_data),
    .out({multiplexer_2_out_2, multiplexer_2_out}), .sel(Instructions_data_2[35:32]));  // open: in10, in11, in12, in13, in14, in15
  Register #(.width(1)) CONDITION (
    .D(multiplexer_2_out[0]), .en(demultiplexer_1_out11), .clk(clock_1_out), .Q(CONDITION_q), .clr(and_1_out));
  Register #(.width(24)) START_DIR (
    .D(multiplexer_2_out), .en(demultiplexer_1_out12), .clk(clock_1_out), .Q(START_DIR_q), .clr(and_1_out));
  Register #(.width(24)) END_DIR (
    .D(multiplexer_2_out), .en(demultiplexer_1_out13), .clk(clock_1_out), .Q(END_DIR_q), .clr(and_1_out));
  Hex_Digit_Display hex_digit_display_32 (.value(binary_to_bcd_converter_9_p1));  // open: dp
  Register #(.width(10)) GPU_INS_ADR (
    .D(multiplexer_2_out[9:0]), .en(demultiplexer_1_out18), .clk(clock_1_out), .Q(GPU_INS_ADR_q),
    .clr(and_1_out));
  Register #(.width(32)) R6 (
    .D({multiplexer_2_out_2, multiplexer_2_out}), .en(demultiplexer_1_out8), .clk(clock_1_out), .Q(R6_q),
    .clr(and_1_out));
  Comparator #(.width(1)) comparator_4 (.a(CONDITION_q), .b(1'b1), .eq(comparator_4_eq));  // open: gt, lt
  Hex_Digit_Display hex_digit_display_33 (.value(binary_to_bcd_converter_9_p3));  // open: dp
  Hex_Digit_Display hex_digit_display_34 (.value(binary_to_bcd_converter_9_p4));  // open: dp
  // Binary_to_BCD_converter #(.binvalue(10)) binary_to_bcd_converter_9: pin names not known; wires that end beside it: binary_to_bcd_converter_9_p1, multiplexer_1_out, binary_to_bcd_converter_9_p3, binary_to_bcd_converter_9_p4, binary_to_bcd_converter_9_p5, binary_to_bcd_converter_9_p6
  Register #(.width(32)) R7 (
    .D({multiplexer_2_out_2, multiplexer_2_out}), .en(demultiplexer_1_out9), .clk(clock_1_out), .Q(R7_q),
    .clr(and_1_out));
  Register #(.width(2)) PC_JUMP_OP (
    .D({multiplexer_2_out[2], multiplexer_2_out[0]}), .en(demultiplexer_1_out17), .clk(clock_1_out),
    .Q(PC_JUMP_OP_q), .clr(and_1_out));
  Multiplexer #(.width(24)) multiplexer_3 (
    .in0(START_DIR_q), .in1(END_DIR_q), .out(multiplexer_3_out), .sel(comparator_4_eq));
  Hex_Digit_Display hex_digit_display_35 (.value(binary_to_bcd_converter_9_p5));  // open: dp
  Multiplexer #(.width(10)) multiplexer_4 (
    .in0(GPU_PC_q_2), .in1(GPU_INS_ADR_q), .out(multiplexer_4_out), .sel(demultiplexer_1_out10));
  Multiplexer #(.select(2), .width(24)) multiplexer_5 (
    .in0(multiplexer_2_out), .in1(STACK_PC_dout), .in2(multiplexer_3_out), .out(multiplexer_5_out),
    .sel(PC_JUMP_OP_q));  // open: in3
  Hex_Digit_Display hex_digit_display_36 (.value(binary_to_bcd_converter_9_p6));  // open: dp
  RAM #(.addrWidth(10), .dataWidth(7)) GPU_INSTRUCTION (
    .addr(multiplexer_4_out), .we(demultiplexer_3_out1), .oe(demultiplexer_3_out0), .clk(clock_1_out),
    .din(multiplexer_2_out[6:0]), .dout(GPU_INSTRUCTION_dout));
  Demultiplexer demultiplexer_3 (
    .out0(demultiplexer_3_out0), .out1(demultiplexer_3_out1), .in(1'b1), .sel(demultiplexer_1_out10));
  Counter #(.max('hffff), .width(16)) GPU_PC (
    .Q({GPU_PC_q_2[9:5], GPU_PC_q[10:8], GPU_PC_q_2[4:0], GPU_PC_q[2:0]}), .up(1'b1), .clk(and_3_out),
    .clr(and_1_out));  // open: load, D, count, carry
  ROM #(.addrWidth(7), .dataWidth(64), .misaligned("true")) Resources (
    .addr(GPU_INSTRUCTION_dout), .data(Resources_data));
  // RGB_Video #(.height(256), .width(256)) rgb_video_1: pin names not known; wires that end beside it: and_1_out, clock_1_out, 1'b1, {GPU_PC_q_2[4:0], GPU_PC_q[2:0]}, {GPU_PC_q_2[9:5], GPU_PC_q[10:8]}, rgb_video_1_p6
  Multiplexer #(.select(3), .width(8)) multiplexer_6 (
    .in0(Resources_data[7:0]), .in1(Resources_data[15:8]), .in2(Resources_data[23:16]),
    .in3(Resources_data[31:24]), .in4(Resources_data[39:32]), .in5(Resources_data[47:40]),
    .in6(Resources_data[55:48]), .in7(Resources_data[63:56]), .out(multiplexer_6_out), .sel(GPU_PC_q[10:8]));
  Multiplexer #(.select(3)) multiplexer_7 (
    .in0(multiplexer_6_out[0]), .in1(multiplexer_6_out[1]), .in2(multiplexer_6_out[2]),
    .in3(multiplexer_6_out[3]), .in4(multiplexer_6_out[4]), .in5(multiplexer_6_out[5]),
    .in6(multiplexer_6_out[6]), .in7(multiplexer_6_out[7]), .out(multiplexer_7_out), .sel(GPU_PC_q[2:0]));
  Multiplexer #(.width(24)) multiplexer_8 (
    .in0({24{1'b0}}), .in1({24{1'b1}}), .out(rgb_video_1_p6), .sel(multiplexer_7_out));

  // Notes on the sheet:
  //   Y
  //   X
  //   contents of Instructions (hex, n*v repeats v):
  //   25900000000 1590000004c 25900000001 15900000012 25900000002 15900000031 25900000003 15900000020
  //   25900000004 15900000000 25900000005 1590000001f 25900000006 15900000020 25900000007 1590000002f
  //   25900000008 15900000020 25900000009 1590000001c 2590000000a 15900000000 2590000000b 1590000002e
  //   2590000000c 15900000020 2590000000d 1590000001c 2590000000e 15900000027 2590000000f 15900000024
  //   25900000010 15900000036 25900000011 1590000001c 25900000012 1590000002e 25900000013 1590000004b
  //   1900000100 3900000008 21900000003
  //   R
  //   contents of Resources (hex, n*v repeats v):
  //   0 41417f4141413e00 3f41413f41413f00 3e41010101413e00 1f21414141211f00 7f01017f01017f00
  //   101017f01017f00 3c42417901423c00 4141417f41414100 7f08080808087f00 1c22202020202000 4141211f21414100
  //   7e02020202020200 4141414149556300 4161514945434100 6151494543007f00 3e41414141413e00 1013f4141413f00
  //   5e21414141413e00 41413f4141413f00 3e41403e01413e00 808080808087f00 3e41414141414100 814142222414100
  //   142a2a4141414100 4141221c22414100 3e41407e41414100 7f01021c20407f00 e111e100e000000 f11110f01010100
  //   e1101110e000000 1e11111e10101000 1e011f110e000000 1010f0101110e00 e11101e11110e00 1111110f01010100
  //   808080800080000 e11101010001000 909070909010000 601010101010100 494949493f000000 242424241c000000
  //   2424241c003c0000 e1111110e000000 101010f11110e00 1010101e11110e00 10101130d000000 1f201e013e000000
  //   182404041f040400 e11111111000000 40a111111000000 a15151111000000 909060909000000 e101e1111110000
  //   1f010e101f000000 3e0808080a0c0800 7e020c3040423c00 1e20201e20201e00 2020203e22242400
  //   3c42403c02027e00 18241c0424241800 404080810203e00 3c42423c42423c00 1824203824241800 3c42464a72423c00
  //   808087f08080800 7f00000000 492a1c7f1c2a4900 202040408080000 400000000000000 204000000000000
  //   400000000040000 204000000040000 4000404040404000 202020202000200 4000408080a0400 2050101020002000
  //   a0a0a00 2020200 143e143e14000000 81e281c0a3c0800 7e00007e000000 2010080408102000 408102010080400
  //   4020202020204000 204040404040200 6020202020206000 604040404040600 2152240812254200 40a0400
  //   7f00000000000000 324c000000 1c023a3a221c0000 6010101810106000 304040c04040300 110a0400
  //   4040202010100000 5c22521c22221c00 808080808080800
endmodule
